// Logisim project karnuh.circ as structural Verilog: 1 circuit, main circuit main
module main (
  input  in_1,
  input  in_2,
  input  in_3,
  input  in_4,
  input  in_5,
  input  in_6,
  input  in_7,
  input  in_8,
  input  in_9,
  input  in_10,
  output out_11
);

  wire and_1_out, and_2_out, and_3_out, and_4_out, not_1_out, not_2_out, not_3_out, not_4_out, not_5_out,
       not_6_out, not_7_out, not_8_out, not_9_out, not_10_out;

  not not_1 (not_1_out, in_1);
  not not_2 (not_2_out, in_2);
  not not_3 (not_3_out, in_3);
  not not_4 (not_4_out, in_4);
  not not_5 (not_5_out, in_5);
  and and_1 (and_1_out, not_1_out, in_3, in_4);
  and and_2 (and_2_out, in_1, not_2_out, in_4);
  and and_3 (and_3_out, not_1_out, in_2, not_3_out, not_4_out);
  and and_4 (and_4_out, in_1, in_3, in_4, in_5);
  or or_1 (out_11, and_1_out, and_2_out, and_3_out, and_4_out);
  not not_6 (not_6_out, in_6);
  not not_7 (not_7_out, in_7);
  not not_8 (not_8_out, in_9);
  not not_9 (not_9_out, in_8);
  not not_10 (not_10_out, in_10);
  // OR_Gate or_2 is placed but not wired
  // OR_Gate or_3 is placed but not wired
  // OR_Gate or_4 is placed but not wired
  // OR_Gate or_5 is placed but not wired
  // AND_Gate and_5 is placed but not wired
endmodule
